# Fritzing sketch RACME (saved by Fritzing 0.9.3b)
breadboards: 1

parts:
  Componente2 = Soil Moisture Sensor
  Componente3 = GUVA-S12SD UV Light Sensor
  RHT1 = Humidity and Temperature Sensor RHT03
  Componente1 = Arduino Uno (Rev3) - ICSP
  M2 = DC Motor
  Power_plug1 = Power plug
  Relay_5V1 = Keyes Relay [package=THT]

nets:
  N1: Componente2.SIG, Componente1.A1
  GND: Componente2.GND, Componente3.GND, RHT1.GND_2, Componente1.GND, Relay_5V1.signal
  VCC: Componente2.VCC, Componente3.5V, RHT1.Vcc, Componente1.5V, Relay_5V1.power
  N2: Componente3.Out, Componente1.A0
  N3: RHT1.Data-signal, RHT1.GND_1, Componente1.D7
  N4: Componente1.D2, Relay_5V1.ground
  N5: M2.pin_1, Power_plug1.VCC
  N6: M2.pin_2, Relay_5V1.NC
  N7: Power_plug1.GND, Relay_5V1.NO

notes:
  Pump
  12V

custom parts:
  GUVA-S12SD UV Light Sensor: Extend your light-sensing spectrum with this analog UV sensor module. It uses a UV photodiode, which can detect the 240-370nm range of light (which covers UVB and most of UVA spectrum). The signal level from the photodiode is very small, in the nano-ampere level, so we tossed on an opamp to amplify the signal to a more manageable volt-level.
  Keyes Relay: The Keyes 5V relay module is suitable for SCM development, home appliance control. It uses a 5V~12V TIL control signal which can control DC / AC signal.
